# Fritzing sketch Roomba_Wiring (saved by Fritzing 0.9.10b)

parts:
  U1 = ESP8266 WiFi Module [part_number=ESP8266]
  Q1 = PNP-Transistor [package="TO92 [THT]"]
  U3 = DIN7 [package=din7]  # not connected
  U4 = ISL29102 [package=odfn6]
  U5 = Buck Converter [package=odfn6]

nets:
  N1: U1.RXD, Q1.C
  N2: U1.VCC, U1.CH_PD, U4.REXT, U5.Roomba_-
  N3: U1.GND, Q1.E, U4.VOUT, U5.ESP_-
  N4: U4.NC, U5.Roomba_+

notes:
  PNP
  Transistor
  ESP-01
  Roomba
  OI Port
  Buck Converter 3.3v

custom parts:
  ESP8266 WiFi Module: Generic WiFi Module based on the ESP8266 with onboard PCB antenna and UART communications
